# Fritzing sketch Motor7esp32s_200729x (saved by Fritzing 0.9.3b)
circuit board: 2.52236cm x 4.88871cm
circuit board: 3.07073cm x 6.39618cm
circuit board: 0.775476cm x 0.914952cm

parts:
  R2 = Resistor [tolerance=±5% resistance=10k package=THT]
  R3 = Resistor [tolerance=±5% resistance=10k package=THT]
  C1 = Electrolytic Capacitor [capacitance=47µF package="100 mil [THT, electrolytic]"]
  R5 = Resistor [tolerance=±5% resistance=100 package=THT]
  R6 = Resistor [tolerance=±5% resistance=100 package=THT]
  L1 = Inductor [package="400 mil [THT]"]
  L2 = Inductor [package="400 mil [THT]"]
  R7 = Resistor [tolerance=±5% resistance=10k package=THT]
  R8 = Resistor [tolerance=±5% resistance=470 package=THT]
  Q2 = PHOTOTRANSISTOR REFLECTIVE OBJECT SENSOR [package=qrb1114-side]
  U1 = TLP621 [package=THT]
  R9 = Resistor [tolerance=±5% resistance=4.7k package=THT]
  R10 = Resistor [tolerance=±5% resistance=47k package=THT]
  R11 = Resistor [tolerance=±5% resistance=47k package=THT]
  R12 = Resistor [tolerance=±5% resistance=10k package=THT]
  DS1 = DS18B20 1-Wire Temperature Sensor [part_number=DS18B20]
  IC1 = Voltage Regulator [part_number=7805 package=to220-igo]
  C2 = Ceramic Capacitor [capacitance=100nF package="200 mil [THT, multilayer]"]

nets:
  3,3V: R2.Pin_0, R7.Pin_0, R8.Pin_0, R9.Pin_0, R12.Pin_1, DS1.VDD
  N1: R2.Pin_1, R3.Pin_0, C1.+, R5.Pin_1, R6.Pin_1, L1.pin_1, L2.pin_1
  GND: R3.Pin_1, C1.-, Q2.E, Q2.K, U1.Pin_3, DS1.GND, IC1.GND, C2.1
  A1 (GPIO32): R5.Pin_0, L2.pin_0
  A2 (GPIO33): R6.Pin_0, L1.pin_0
  A0 (GPIO36): R7.Pin_1, Q2.C
  N2: R8.Pin_1, Q2.A
  N3: U1.Pin_1, R10.Pin_0
  N4: U1.Pin_2, R11.Pin_0
  N5: U1.Pin_4, R9.Pin_1
  N6: R12.Pin_0, DS1.DQ
  N7: IC1.OUT, C2.0

notes:
  Motor7esp32s_200729x
